// Logisim project Project_1_ECS154A.circ as structural Verilog
module main (
  input  in_1,
  input  in_2,
  input  in_3,
  input  in_4,
  input  in_5
);

  wire compare_1_e, compare_1_n, fiveseven_1_a, fiveseven_1_b, fiveseven_1_c, fiveseven_1_d, fiveseven_1_e,
       fiveseven_1_f, fiveseven_1_g;

  FiveSeven fiveseven_1 (
    .V(in_1), .W(in_2), .X(in_3), .Y(in_4), .Z(in_5), .A(fiveseven_1_a), .B(fiveseven_1_b),
    .C(fiveseven_1_c), .D(fiveseven_1_d), .E(fiveseven_1_e), .F(fiveseven_1_f), .G(fiveseven_1_g));
  _7_Segment_Display #(.decimalPoint("false")) u_7_segment_display_1 (
    .g(fiveseven_1_g), .f(fiveseven_1_f), .a(fiveseven_1_a), .b(fiveseven_1_b), .e(fiveseven_1_e),
    .d(fiveseven_1_d), .c(fiveseven_1_c));
  LED Equal (.in(compare_1_e));
  Compare compare_1 (
    .X0(1'b0), .X1(1'b0), .X2(1'b0), .Y0(1'b0), .Y1(1'b0), .Y2(1'b0), .E(compare_1_e), .N(compare_1_n));
  LED Not_Equal (.in(compare_1_n));
endmodule

module Compare (
  input  X0,
  input  X1,
  input  X2,
  input  Y0,
  input  Y1,
  input  Y2,
  output E,
  output N
);

  wire [2:0] xnor_1_out;

  assign xnor_1_out = ~({X2, X1, X0} ^ {Y2, Y1, Y0});  // XNOR_Gate xnor_1, 3 bits wide
  and and_1 (E, xnor_1_out[0], xnor_1_out[1], xnor_1_out[2]);
  not not_1 (N, E);
endmodule

module FiveSeven (
  input  V,
  input  W,
  input  X,
  input  Y,
  input  Z,
  output A,
  output B,
  output C,
  output D,
  output E,
  output F,
  output G
);

  wire and_7_out, and_9_out, and_10_out, and_12_out, and_14_out, Eight, Five, Four, Nine, nor_1_out, One,
       or_1_out, or_2_out, or_3_out, or_4_out, or_5_out, or_6_out, Seven, Six, Three, Two, xor_1_out,
       xor_2_out, xor_3_out, xor_4_out, xor_5_out, xor_6_out, Zero;

  and and_1 (Five, nor_1_out, Z);
  and and_2 (Zero, ~Z, nor_1_out);  // AND_Gate
  nor nor_1 (nor_1_out, V, Y, X, W);
  and and_3 (Six, Z, xor_1_out);
  and and_4 (One, ~Z, xor_1_out);  // AND_Gate
  ExactlyOne xor_1 (.out(xor_1_out), .in0(W), .in1(X), .in2(Y), .in3(V));
  and and_5 (Two, ~Z, xor_4_out);  // AND_Gate
  or or_1 (or_1_out, V, W);
  or or_2 (or_2_out, X, Y);
  xor xor_2 (xor_2_out, or_1_out, or_2_out);
  or or_3 (or_3_out, V, X);
  or or_4 (or_4_out, W, Y);
  xor xor_3 (xor_3_out, or_3_out, or_4_out);
  ExactlyOne xor_4 (.out(xor_4_out), .in0(xor_2_out), .in1(xor_3_out), .in2(xor_5_out));
  and and_6 (Seven, Z, xor_4_out);
  or or_5 (or_5_out, V, Y);
  or or_6 (or_6_out, W, X);
  xor xor_5 (xor_5_out, or_5_out, or_6_out);
  and and_7 (and_7_out, V, W, X);
  and and_8 (Three, ~Z, xor_6_out);  // AND_Gate
  and and_9 (and_9_out, W, X, Y);
  and and_10 (and_10_out, V, X, Y);
  ExactlyOne xor_6 (.out(xor_6_out), .in0(and_7_out), .in1(and_9_out), .in2(and_10_out), .in3(and_12_out));
  and and_11 (Eight, Z, xor_6_out);
  and and_12 (and_12_out, V, W, Y);
  and and_13 (Nine, Z, and_14_out);
  and and_14 (and_14_out, Y, X, W, V);
  and and_15 (Four, ~Z, and_14_out);  // AND_Gate
  or or_7 (A, Zero, Two, Three, Five, Six, Seven, Eight, Nine);
  or or_8 (B, Zero, One, Two, Three, Four, Seven, Eight, Nine);
  or or_9 (C, Zero, One, Three, Four, Five, Six, Seven, Eight, Nine);
  or or_10 (D, Zero, Two, Three, Five, Six, Eight, Nine);
  or or_11 (E, Zero, Two, Six, Eight);
  or or_12 (F, Six, Four, Five, Eight, Nine, Zero);
  or or_13 (G, Two, Three, Four, Five, Six, Eight, Nine);
endmodule
